// Digital circuit mux2sv.dig as structural Verilog
module mux2sv (
  input  S,
  output [1:0] Y
);

  mux2 #(.applicationType("IVERILOG"), .iverilogOptions("-g2005-sv"), .CodeFile("/home/josan/mux2.sv")) u_mux2 (
    .d0(2'b01), .d1(2'b10), .s(S), .y(Y));
endmodule
