// Digital circuit mux2sv2.dig as structural Verilog
module mux2sv2 (
  input  S,
  output [7:0] Y
);

  mux2 #(.applicationType("IVERILOG"), .iverilogOptions("-g2005-sv"), .CodeFile("/home/josan/mux22.sv")) u_mux2 (
    .d0(8'h1), .d1(8'h2), .s(S), .y(Y));
endmodule
