// Digital circuit mux4sv.dig as structural Verilog
module mux4sv (
  input  [1:0] S,
  output [11:0] Y
);

  mux4 #(.applicationType("IVERILOG"), .iverilogOptions("-g2005-sv"), .CodeFile("/home/josan/mux4.sv")) u_mux4 (
    .d0(12'ha), .d1(12'h5), .d2(12'h5), .d3(12'ha), .s(S), .y(Y));
endmodule
